// Logisim project proj.circ as structural Verilog: 3 circuits, main circuit main
module main (
);

  wire clock_1_out, down, left, right, up;
  wire [31:0] map_1_out_8, map_1_out_9, map_1_out_10, map_1_out_11, map_1_out_12, map_1_out_13, map_1_out_14,
       map_1_out_15, map_1_out_16, map_1_out_17, map_1_out_18, map_1_out_19, map_1_out_20, map_1_out_21,
       map_1_out_22, map_1_out_23, map_1_out_24, map_1_out_25, map_1_out_26, map_1_out_27, map_1_out_28,
       map_1_out_29, map_1_out_30, map_1_out_31, map_1_out_32, map_1_out_33, map_1_out_34, map_1_out_35,
       map_1_out_36, map_1_out_37, map_1_out_38, map_1_out_39;

  Clock clock_1 (.out(clock_1_out));
  DotMatrix #(.inputtype("row"), .matrixcols(32), .matrixrows(32)) dotmatrix_1 (
    .row0(map_1_out_8), .row1(map_1_out_9), .row2(map_1_out_10), .row3(map_1_out_11), .row4(map_1_out_12),
    .row5(map_1_out_13), .row6(map_1_out_14), .row7(map_1_out_15), .row8(map_1_out_16), .row9(map_1_out_17),
    .row10(map_1_out_18), .row11(map_1_out_19), .row12(map_1_out_20), .row13(map_1_out_21),
    .row14(map_1_out_22), .row15(map_1_out_23), .row16(map_1_out_24), .row17(map_1_out_25),
    .row18(map_1_out_26), .row19(map_1_out_27), .row20(map_1_out_28), .row21(map_1_out_29),
    .row22(map_1_out_30), .row23(map_1_out_31), .row24(map_1_out_32), .row25(map_1_out_33),
    .row26(map_1_out_34), .row27(map_1_out_35), .row28(map_1_out_36), .row29(map_1_out_37),
    .row30(map_1_out_38), .row31(map_1_out_39));
  map map_1 (
    .in_2(down), .in_3(up), .in_5(left), .in_6(right), .shift(clock_1_out), .in_4(32'h18000),
    .out_8(map_1_out_8), .out_9(map_1_out_9), .out_10(map_1_out_10), .out_11(map_1_out_11),
    .out_12(map_1_out_12), .out_13(map_1_out_13), .out_14(map_1_out_14), .out_15(map_1_out_15),
    .out_16(map_1_out_16), .out_17(map_1_out_17), .out_18(map_1_out_18), .out_19(map_1_out_19),
    .out_20(map_1_out_20), .out_21(map_1_out_21), .out_22(map_1_out_22), .out_23(map_1_out_23),
    .out_24(map_1_out_24), .out_25(map_1_out_25), .out_26(map_1_out_26), .out_27(map_1_out_27),
    .out_28(map_1_out_28), .out_29(map_1_out_29), .out_30(map_1_out_30), .out_31(map_1_out_31),
    .out_32(map_1_out_32), .out_33(map_1_out_33), .out_34(map_1_out_34), .out_35(map_1_out_35),
    .out_36(map_1_out_36), .out_37(map_1_out_37), .out_38(map_1_out_38), .out_39(map_1_out_39));  // open: end
  Button button_1 (.out(up));
  Button button_2 (.out(left));
  Button button_3 (.out(right));
  Button button_4 (.out(down));
endmodule

module map (
  input  \end ,
  input  in_2,
  input  in_3,
  input  [31:0] in_4,
  input  in_5,
  input  in_6,
  input  shift,
  output [31:0] out_8,
  output [31:0] out_9,
  output [31:0] out_10,
  output [31:0] out_11,
  output [31:0] out_12,
  output [31:0] out_13,
  output [31:0] out_14,
  output [31:0] out_15,
  output [31:0] out_16,
  output [31:0] out_17,
  output [31:0] out_18,
  output [31:0] out_19,
  output [31:0] out_20,
  output [31:0] out_21,
  output [31:0] out_22,
  output [31:0] out_23,
  output [31:0] out_24,
  output [31:0] out_25,
  output [31:0] out_26,
  output [31:0] out_27,
  output [31:0] out_28,
  output [31:0] out_29,
  output [31:0] out_30,
  output [31:0] out_31,
  output [31:0] out_32,
  output [31:0] out_33,
  output [31:0] out_34,
  output [31:0] out_35,
  output [31:0] out_36,
  output [31:0] out_37,
  output [31:0] out_38,
  output [31:0] out_39
);

  wire [1:0] counter_5_q;
  wire [4:0] counter_1_q, counter_2_q, counter_3_q, counter_4_q, random_1_out, subtractor_1_out;
  wire [31:0] demultiplexer_1_out0, demultiplexer_1_out1, demultiplexer_1_out2, demultiplexer_1_out3,
       demultiplexer_1_out4, demultiplexer_1_out5, demultiplexer_1_out6, demultiplexer_1_out7,
       demultiplexer_1_out8, demultiplexer_1_out9, demultiplexer_1_out10, demultiplexer_1_out11,
       demultiplexer_1_out12, demultiplexer_1_out13, demultiplexer_1_out14, demultiplexer_1_out15,
       demultiplexer_1_out16, demultiplexer_1_out17, demultiplexer_1_out18, demultiplexer_1_out19,
       demultiplexer_1_out20, demultiplexer_1_out21, demultiplexer_1_out22, demultiplexer_1_out23,
       demultiplexer_1_out24, demultiplexer_1_out25, demultiplexer_1_out26, demultiplexer_1_out27,
       demultiplexer_1_out28, demultiplexer_1_out29, demultiplexer_1_out30, demultiplexer_1_out31,
       multiplexer_1_out, shifter_1_out, shifter_2_out, shifter_3_out, str0, str1, str2, str3, str4, str5,
       str6, str7, str8, str9, str10, str11, str12, str13, str14, str15, str16, str17, str18, str19, str20,
       str21, str22, str23, str24, str25, str26, str27, str28, str29, str30, str31;

  Counter #(.width(5), .max('h1f)) counter_1 (.Q(counter_1_q), .clk(in_2));  // open: load, D, count, carry, clr
  Counter #(.width(5), .max('h1f)) counter_2 (.Q(counter_2_q), .clk(in_3));  // open: load, D, count, carry, clr
  Counter #(.width(5), .max('h1f)) counter_3 (.Q(counter_3_q), .clk(in_5));  // open: load, D, count, carry, clr
  Counter #(.width(5), .max('h1f)) counter_4 (.Q(counter_4_q), .clk(in_6));  // open: load, D, count, carry, clr
  Subtractor #(.width(5)) subtractor_1 (.a(counter_1_q), .b(counter_2_q), .out(subtractor_1_out));  // open: bin, bout
  Shifter #(.width(32), .shift("rl")) shifter_1 (.in(in_4), .\dist (counter_3_q), .out(shifter_1_out));
  Shifter #(.width(32), .shift("rr")) shifter_2 (.in(shifter_1_out), .\dist (counter_4_q), .out(shifter_2_out));
  Demultiplexer #(.select(5), .width(32), .enable("false")) demultiplexer_1 (
    .out0(demultiplexer_1_out0), .out1(demultiplexer_1_out1), .out2(demultiplexer_1_out2),
    .out3(demultiplexer_1_out3), .out4(demultiplexer_1_out4), .out5(demultiplexer_1_out5),
    .out6(demultiplexer_1_out6), .out7(demultiplexer_1_out7), .out8(demultiplexer_1_out8),
    .out9(demultiplexer_1_out9), .out10(demultiplexer_1_out10), .out11(demultiplexer_1_out11),
    .out12(demultiplexer_1_out12), .out13(demultiplexer_1_out13), .out14(demultiplexer_1_out14),
    .out15(demultiplexer_1_out15), .out16(demultiplexer_1_out16), .out17(demultiplexer_1_out17),
    .out18(demultiplexer_1_out18), .out19(demultiplexer_1_out19), .out20(demultiplexer_1_out20),
    .out21(demultiplexer_1_out21), .out22(demultiplexer_1_out22), .out23(demultiplexer_1_out23),
    .out24(demultiplexer_1_out24), .out25(demultiplexer_1_out25), .out26(demultiplexer_1_out26),
    .out27(demultiplexer_1_out27), .out28(demultiplexer_1_out28), .out29(demultiplexer_1_out29),
    .out30(demultiplexer_1_out30), .out31(demultiplexer_1_out31), .in(shifter_2_out), .sel(subtractor_1_out));
  // Probe on shifter_2_out
  assign out_8 = str0 | demultiplexer_1_out0;  // OR_Gate or_1, 32 bits wide
  assign out_9 = str1 | demultiplexer_1_out1;  // OR_Gate or_2, 32 bits wide
  assign out_10 = str2 | demultiplexer_1_out2;  // OR_Gate or_3, 32 bits wide
  assign out_11 = str3 | demultiplexer_1_out3;  // OR_Gate or_4, 32 bits wide
  assign out_12 = str4 | demultiplexer_1_out4;  // OR_Gate or_5, 32 bits wide
  assign out_13 = str5 | demultiplexer_1_out5;  // OR_Gate or_6, 32 bits wide
  assign out_14 = str6 | demultiplexer_1_out6;  // OR_Gate or_7, 32 bits wide
  assign out_15 = str7 | demultiplexer_1_out7;  // OR_Gate or_8, 32 bits wide
  assign out_16 = str8 | demultiplexer_1_out8;  // OR_Gate or_9, 32 bits wide
  assign out_17 = str9 | demultiplexer_1_out9;  // OR_Gate or_10, 32 bits wide
  assign out_18 = str10 | demultiplexer_1_out10;  // OR_Gate or_11, 32 bits wide
  assign out_19 = str11 | demultiplexer_1_out11;  // OR_Gate or_12, 32 bits wide
  assign out_20 = str12 | demultiplexer_1_out12;  // OR_Gate or_13, 32 bits wide
  assign out_21 = str13 | demultiplexer_1_out13;  // OR_Gate or_14, 32 bits wide
  assign out_22 = str14 | demultiplexer_1_out14;  // OR_Gate or_15, 32 bits wide
  assign out_23 = str15 | demultiplexer_1_out15;  // OR_Gate or_16, 32 bits wide
  assign out_24 = str16 | demultiplexer_1_out16;  // OR_Gate or_17, 32 bits wide
  assign out_25 = str17 | demultiplexer_1_out17;  // OR_Gate or_18, 32 bits wide
  assign out_26 = str18 | demultiplexer_1_out18;  // OR_Gate or_19, 32 bits wide
  assign out_27 = str19 | demultiplexer_1_out19;  // OR_Gate or_20, 32 bits wide
  assign out_28 = str20 | demultiplexer_1_out20;  // OR_Gate or_21, 32 bits wide
  assign out_29 = str21 | demultiplexer_1_out21;  // OR_Gate or_22, 32 bits wide
  assign out_30 = str22 | demultiplexer_1_out22;  // OR_Gate or_23, 32 bits wide
  assign out_31 = str23 | demultiplexer_1_out23;  // OR_Gate or_24, 32 bits wide
  assign out_32 = str24 | demultiplexer_1_out24;  // OR_Gate or_25, 32 bits wide
  assign out_33 = str25 | demultiplexer_1_out25;  // OR_Gate or_26, 32 bits wide
  assign out_34 = str26 | demultiplexer_1_out26;  // OR_Gate or_27, 32 bits wide
  assign out_35 = str27 | demultiplexer_1_out27;  // OR_Gate or_28, 32 bits wide
  assign out_36 = str28 | demultiplexer_1_out28;  // OR_Gate or_29, 32 bits wide
  assign out_37 = str29 | demultiplexer_1_out29;  // OR_Gate or_30, 32 bits wide
  assign out_38 = str30 | demultiplexer_1_out30;  // OR_Gate or_31, 32 bits wide
  assign out_39 = str31 | demultiplexer_1_out31;  // OR_Gate or_32, 32 bits wide
  Random #(.width(5)) random_1 (.clk(shift), .out(random_1_out));  // open: next, clr
  Shifter #(.width(32)) shifter_3 (.in(32'hf), .\dist (random_1_out), .out(shifter_3_out));
  Counter #(.width(2), .max('h3)) counter_5 (.Q(counter_5_q), .clk(shift));  // open: load, D, count, carry, clr
  Multiplexer #(.select(2), .width(32), .enable("false")) multiplexer_1 (
    .in0(shifter_3_out), .in1({32{1'b0}}), .in2({32{1'b0}}), .in3({32{1'b0}}), .out(multiplexer_1_out),
    .sel(counter_5_q));
  Shift_Register #(.width(32), .length(32)) shift_register_1 (
    .shift(1'b1), .in(multiplexer_1_out), .clk(shift), .load(\end ), .d0(32'h3c000), .q0(str0),
    .d1({32{1'b0}}), .q1(str1), .d2({32{1'b0}}), .q2(str2), .d3({32{1'b0}}), .q3(str3), .d4({32{1'b0}}),
    .q4(str4), .d5({32{1'b0}}), .q5(str5), .d6({32{1'b0}}), .q6(str6), .d7({32{1'b0}}), .q7(str7),
    .d8({32{1'b0}}), .q8(str8), .d9({32{1'b0}}), .q9(str9), .d10({32{1'b0}}), .q10(str10), .d11({32{1'b0}}),
    .q11(str11), .d12({32{1'b0}}), .q12(str12), .d13({32{1'b0}}), .q13(str13), .d14({32{1'b0}}), .q14(str14),
    .d15({32{1'b0}}), .q15(str15), .d16({32{1'b0}}), .q16(str16), .d17({32{1'b0}}), .q17(str17),
    .d18({32{1'b0}}), .q18(str18), .d19({32{1'b0}}), .q19(str19), .d20({32{1'b0}}), .q20(str20),
    .d21({32{1'b0}}), .q21(str21), .d22({32{1'b0}}), .q22(str22), .d23({32{1'b0}}), .q23(str23),
    .d24({32{1'b0}}), .q24(str24), .d25({32{1'b0}}), .q25(str25), .d26({32{1'b0}}), .q26(str26),
    .d27({32{1'b0}}), .q27(str27), .d28({32{1'b0}}), .q28(str28), .d29({32{1'b0}}), .q29(str29),
    .d30({32{1'b0}}), .q30(str30), .d31({32{1'b0}}), .q31(str31));  // open: out, clr
endmodule

module isW (
  output out_1
);

  wire comparator_1_eq, comparator_2_eq;
  wire [6:0] keyboard_1_data;

  Keyboard keyboard_1 (.clk(1'b1), .data(keyboard_1_data));  // open: re, clr, avail
  Comparator #(.width(7)) comparator_1 (.a(7'b1010111), .b(keyboard_1_data), .eq(comparator_1_eq));  // open: gt, lt
  Comparator #(.width(7)) comparator_2 (.a(keyboard_1_data), .b(7'b1110111), .eq(comparator_2_eq));  // open: gt, lt
  or or_1 (out_1, comparator_1_eq, comparator_2_eq);
endmodule
